// Logisim project BullsAndCows.circ as structural Verilog: 1 circuit, main circuit main
module main (
);

  wire _0, _1, _2, _3, _4, _5, _6, _7, _8, _9, Clock, d0_t, d1_t, d2_t, d3_t, dead, Ent, game, invalid, lose,
       match, n7_seg_decoder_1_a, n7_seg_decoder_1_b, n7_seg_decoder_1_c, n7_seg_decoder_1_d,
       n7_seg_decoder_1_e, n7_seg_decoder_1_f, n7_seg_decoder_1_g, n7_seg_decoder_2_a, n7_seg_decoder_2_b,
       n7_seg_decoder_2_c, n7_seg_decoder_2_d, n7_seg_decoder_2_e, n7_seg_decoder_2_f, n7_seg_decoder_2_g,
       n7_seg_decoder_3_a, n7_seg_decoder_3_b, n7_seg_decoder_3_c, n7_seg_decoder_3_d, n7_seg_decoder_3_e,
       n7_seg_decoder_3_f, n7_seg_decoder_3_g, n7_seg_decoder_4_a, n7_seg_decoder_4_b, n7_seg_decoder_4_c,
       n7_seg_decoder_4_d, n7_seg_decoder_4_e, n7_seg_decoder_4_f, n7_seg_decoder_4_g, n7_seg_decoder_5_a,
       n7_seg_decoder_5_b, n7_seg_decoder_5_c, n7_seg_decoder_5_d, n7_seg_decoder_5_e, n7_seg_decoder_5_f,
       n7_seg_decoder_5_g, n7_seg_decoder_6_a, n7_seg_decoder_6_b, n7_seg_decoder_6_c, n7_seg_decoder_6_d,
       n7_seg_decoder_6_e, n7_seg_decoder_6_f, n7_seg_decoder_6_g, n7_seg_decoder_7_a, n7_seg_decoder_7_b,
       n7_seg_decoder_7_c, n7_seg_decoder_7_d, n7_seg_decoder_7_e, n7_seg_decoder_7_f, n7_seg_decoder_7_g,
       n7_seg_decoder_8_a, n7_seg_decoder_8_b, n7_seg_decoder_8_c, n7_seg_decoder_8_d, n7_seg_decoder_8_e,
       n7_seg_decoder_8_f, n7_seg_decoder_8_g, n7_seg_decoder_9_a, n7_seg_decoder_9_b, n7_seg_decoder_9_c,
       n7_seg_decoder_9_d, n7_seg_decoder_9_e, n7_seg_decoder_9_f, n7_seg_decoder_9_g, n7_seg_decoder_10_a,
       n7_seg_decoder_10_b, n7_seg_decoder_10_c, n7_seg_decoder_10_d, n7_seg_decoder_10_e,
       n7_seg_decoder_10_f, n7_seg_decoder_10_g, n7_seg_decoder_11_a, n7_seg_decoder_11_b,
       n7_seg_decoder_11_c, n7_seg_decoder_11_d, n7_seg_decoder_11_e, n7_seg_decoder_11_f,
       n7_seg_decoder_11_g, n7_seg_decoder_12_a, n7_seg_decoder_12_b, n7_seg_decoder_12_c,
       n7_seg_decoder_12_d, n7_seg_decoder_12_e, n7_seg_decoder_12_f, n7_seg_decoder_12_g, R, start, tunnel,
       tunnel_t, \wait , win;
  wire [1:0] digit_selector_digit_place;
  wire [2:0] state;
  wire [3:0] Bulls, Cows, D0, D1, D2, D3, I0, I1, I2, I3, Lives, S0, S1, S2, S3, T0, T1, T2, T3, Wins;
  wire [15:0] random_generator_rand_output;

  Clock clock_1 (.out(Clock));
  LED led_1 (.in(d3_t));
  _7_Segment_Display u_7_segment_display_1 (
    .g(n7_seg_decoder_1_g), .f(n7_seg_decoder_1_f), .a(n7_seg_decoder_1_a), .b(n7_seg_decoder_1_b),
    .e(n7_seg_decoder_1_e), .d(n7_seg_decoder_1_d), .c(n7_seg_decoder_1_c));  // open: dp
  _7_seg_decoder u_7_seg_decoder_1 (
    .\input (D3), .a(n7_seg_decoder_1_a), .b(n7_seg_decoder_1_b), .c(n7_seg_decoder_1_c),
    .d(n7_seg_decoder_1_d), .e(n7_seg_decoder_1_e), .f(n7_seg_decoder_1_f), .g(n7_seg_decoder_1_g));
  Random_generator random_generator (
    .random_button(R), .clock(Clock), .state(state), .Rand_output(random_generator_rand_output));
  digit_selector digit_selector (
    .L(tunnel), .R(tunnel_t), .clock(Clock), .state(state), .Digit_Place(digit_selector_digit_place));
  LED led_2 (.in(d2_t));
  _7_Segment_Display u_7_segment_display_2 (
    .g(n7_seg_decoder_2_g), .f(n7_seg_decoder_2_f), .a(n7_seg_decoder_2_a), .b(n7_seg_decoder_2_b),
    .e(n7_seg_decoder_2_e), .d(n7_seg_decoder_2_d), .c(n7_seg_decoder_2_c));  // open: dp
  _7_seg_decoder u_7_seg_decoder_2 (
    .\input (D2), .a(n7_seg_decoder_2_a), .b(n7_seg_decoder_2_b), .c(n7_seg_decoder_2_c),
    .d(n7_seg_decoder_2_d), .e(n7_seg_decoder_2_e), .f(n7_seg_decoder_2_f), .g(n7_seg_decoder_2_g));
  Digit_input_with_random_input digit_input_with_random_input_1 (
    ._0(_0), ._1(_1), ._2(_2), ._3(_3), ._4(_4), ._5(_5), ._6(_6), ._7(_7), ._8(_8), ._9(_9),
    .random_input(random_generator_rand_output), .random_click(R), .clock(Clock),
    .in_14(digit_selector_digit_place), .State(state), .I0(I0), .I1(I1), .I2(I2), .I3(I3));
  LED led_3 (.in(d1_t));
  _7_Segment_Display u_7_segment_display_3 (
    .g(n7_seg_decoder_3_g), .f(n7_seg_decoder_3_f), .a(n7_seg_decoder_3_a), .b(n7_seg_decoder_3_b),
    .e(n7_seg_decoder_3_e), .d(n7_seg_decoder_3_d), .c(n7_seg_decoder_3_c));  // open: dp
  _7_seg_decoder u_7_seg_decoder_3 (
    .\input (D1), .a(n7_seg_decoder_3_a), .b(n7_seg_decoder_3_b), .c(n7_seg_decoder_3_c),
    .d(n7_seg_decoder_3_d), .e(n7_seg_decoder_3_e), .f(n7_seg_decoder_3_f), .g(n7_seg_decoder_3_g));
  Decoder #(.select(2)) decoder_1 (
    .out0(d0_t), .out1(d1_t), .out2(d2_t), .out3(d3_t), .sel(digit_selector_digit_place));  // open: en
  _7_Segment_Display u_7_segment_display_4 (
    .g(n7_seg_decoder_4_g), .f(n7_seg_decoder_4_f), .a(n7_seg_decoder_4_a), .b(n7_seg_decoder_4_b),
    .e(n7_seg_decoder_4_e), .d(n7_seg_decoder_4_d), .c(n7_seg_decoder_4_c));  // open: dp
  _7_seg_decoder u_7_seg_decoder_4 (
    .\input (D0), .a(n7_seg_decoder_4_a), .b(n7_seg_decoder_4_b), .c(n7_seg_decoder_4_c),
    .d(n7_seg_decoder_4_d), .e(n7_seg_decoder_4_e), .f(n7_seg_decoder_4_f), .g(n7_seg_decoder_4_g));
  Button u__1 (.out(_1));
  Button u__4 (.out(_4));
  Button u__7 (.out(_7));
  Button u_R (.out(R));
  Button button (.out(tunnel));
  LED led_4 (.in(d0_t));
  LED led_5 (.in(invalid));
  Button u__2 (.out(_2));
  Button u__3 (.out(_3));
  Button u__5 (.out(_5));
  Button u__6 (.out(_6));
  Button u__9 (.out(_9));
  Button u__8 (.out(_8));
  Button u__0 (.out(_0));
  Button button_2 (.out(tunnel_t));
  Button button_3 (.out(Ent));
  _7_Segment_Display u_7_segment_display_5 (
    .g(n7_seg_decoder_5_g), .f(n7_seg_decoder_5_f), .a(n7_seg_decoder_5_a), .b(n7_seg_decoder_5_b),
    .e(n7_seg_decoder_5_e), .d(n7_seg_decoder_5_d), .c(n7_seg_decoder_5_c));  // open: dp
  _7_seg_decoder u_7_seg_decoder_5 (
    .\input (S3), .a(n7_seg_decoder_5_a), .b(n7_seg_decoder_5_b), .c(n7_seg_decoder_5_c),
    .d(n7_seg_decoder_5_d), .e(n7_seg_decoder_5_e), .f(n7_seg_decoder_5_f), .g(n7_seg_decoder_5_g));
  _7_Segment_Display u_7_segment_display_6 (
    .g(n7_seg_decoder_6_g), .f(n7_seg_decoder_6_f), .a(n7_seg_decoder_6_a), .b(n7_seg_decoder_6_b),
    .e(n7_seg_decoder_6_e), .d(n7_seg_decoder_6_d), .c(n7_seg_decoder_6_c));  // open: dp
  _7_seg_decoder u_7_seg_decoder_6 (
    .\input (Bulls), .a(n7_seg_decoder_6_a), .b(n7_seg_decoder_6_b), .c(n7_seg_decoder_6_c),
    .d(n7_seg_decoder_6_d), .e(n7_seg_decoder_6_e), .f(n7_seg_decoder_6_f), .g(n7_seg_decoder_6_g));
  LED u_start (.in(start));
  _7_Segment_Display u_7_segment_display_7 (
    .g(n7_seg_decoder_7_g), .f(n7_seg_decoder_7_f), .a(n7_seg_decoder_7_a), .b(n7_seg_decoder_7_b),
    .e(n7_seg_decoder_7_e), .d(n7_seg_decoder_7_d), .c(n7_seg_decoder_7_c));  // open: dp
  _7_seg_decoder u_7_seg_decoder_7 (
    .\input (S2), .a(n7_seg_decoder_7_a), .b(n7_seg_decoder_7_b), .c(n7_seg_decoder_7_c),
    .d(n7_seg_decoder_7_d), .e(n7_seg_decoder_7_e), .f(n7_seg_decoder_7_f), .g(n7_seg_decoder_7_g));
  _7_Segment_Display u_7_segment_display_8 (
    .g(n7_seg_decoder_8_g), .f(n7_seg_decoder_8_f), .a(n7_seg_decoder_8_a), .b(n7_seg_decoder_8_b),
    .e(n7_seg_decoder_8_e), .d(n7_seg_decoder_8_d), .c(n7_seg_decoder_8_c));  // open: dp
  _7_seg_decoder u_7_seg_decoder_8 (
    .\input (Cows), .a(n7_seg_decoder_8_a), .b(n7_seg_decoder_8_b), .c(n7_seg_decoder_8_c),
    .d(n7_seg_decoder_8_d), .e(n7_seg_decoder_8_e), .f(n7_seg_decoder_8_f), .g(n7_seg_decoder_8_g));
  LED u_game (.in(game));
  register_setup_guess setup_and_guess_registers (
    .I0(I0), .I1(I1), .I2(I2), .I3(I3), .Enter(Ent), .Error(invalid), .state(state), .clock(Clock), .s0(S0),
    .s1(S1), .s2(S2), .s3(S3), .t0(T0), .t1(T1), .t2(T2), .t3(T3));
  bulls_cows_error_display bulls__cows__error__displaying_digits (
    .t1(I0), .t2(I1), .t3(I2), .t4(I3), .tr1(T0), .tr2(T1), .tr3(T2), .tr4(T3), .sr1(S0), .sr2(S1), .sr3(S2),
    .sr4(S3), .state(state), .D0(D0), .D1(D1), .D2(D2), .D3(D3), .same_digit(invalid), .match(match),
    .Bulls(Bulls), .Cows(Cows));
  _7_Segment_Display u_7_segment_display_9 (
    .g(n7_seg_decoder_9_g), .f(n7_seg_decoder_9_f), .a(n7_seg_decoder_9_a), .b(n7_seg_decoder_9_b),
    .e(n7_seg_decoder_9_e), .d(n7_seg_decoder_9_d), .c(n7_seg_decoder_9_c));  // open: dp
  _7_seg_decoder u_7_seg_decoder_9 (
    .\input (S1), .a(n7_seg_decoder_9_a), .b(n7_seg_decoder_9_b), .c(n7_seg_decoder_9_c),
    .d(n7_seg_decoder_9_d), .e(n7_seg_decoder_9_e), .f(n7_seg_decoder_9_f), .g(n7_seg_decoder_9_g));
  _7_seg_decoder u_7_seg_decoder_10 (
    .\input (Wins), .a(n7_seg_decoder_10_a), .b(n7_seg_decoder_10_b), .c(n7_seg_decoder_10_c),
    .d(n7_seg_decoder_10_d), .e(n7_seg_decoder_10_e), .f(n7_seg_decoder_10_f), .g(n7_seg_decoder_10_g));
  LED u_wait (.in(\wait ));
  _7_seg_decoder u_7_seg_decoder_11 (
    .\input (S0), .a(n7_seg_decoder_11_a), .b(n7_seg_decoder_11_b), .c(n7_seg_decoder_11_c),
    .d(n7_seg_decoder_11_d), .e(n7_seg_decoder_11_e), .f(n7_seg_decoder_11_f), .g(n7_seg_decoder_11_g));
  _7_Segment_Display u_7_segment_display_10 (
    .g(n7_seg_decoder_10_g), .f(n7_seg_decoder_10_f), .a(n7_seg_decoder_10_a), .b(n7_seg_decoder_10_b),
    .e(n7_seg_decoder_10_e), .d(n7_seg_decoder_10_d), .c(n7_seg_decoder_10_c));  // open: dp
  LED u_win (.in(win));
  _7_Segment_Display u_7_segment_display_11 (
    .g(n7_seg_decoder_11_g), .f(n7_seg_decoder_11_f), .a(n7_seg_decoder_11_a), .b(n7_seg_decoder_11_b),
    .e(n7_seg_decoder_11_e), .d(n7_seg_decoder_11_d), .c(n7_seg_decoder_11_c));  // open: dp
  _7_Segment_Display u_7_segment_display_12 (
    .g(n7_seg_decoder_12_g), .f(n7_seg_decoder_12_f), .a(n7_seg_decoder_12_a), .b(n7_seg_decoder_12_b),
    .e(n7_seg_decoder_12_e), .d(n7_seg_decoder_12_d), .c(n7_seg_decoder_12_c));  // open: dp
  _7_seg_decoder u_7_seg_decoder_12 (
    .\input (Lives), .a(n7_seg_decoder_12_a), .b(n7_seg_decoder_12_b), .c(n7_seg_decoder_12_c),
    .d(n7_seg_decoder_12_d), .e(n7_seg_decoder_12_e), .f(n7_seg_decoder_12_f), .g(n7_seg_decoder_12_g));
  LED u_lose (.in(lose));
  state_to_led_decoder state_decoder (
    .start(start), .game(game), .\wait (\wait ), .win(win), .lose(lose), .state(state), .match(match));
  win_lives_memory_correct wins_and_lives_memory (
    .match(match), .error(invalid), .state(state), .clock(Clock), .wins(Wins), .lives(Lives), .dead(dead));
  Circuit_Controller_w__Error_Check next_state_controller (
    .error(invalid), .zerolives(dead), .win(match), .enter(Ent), .Clock(Clock), .Output(state));
  // Probe on state

  // Other names for the same wires on the sheet: enter = Ent

  // Notes on the sheet:
  //   Members:
  //   Mikhael Dionio 35
  //   Input Buttons
  //   BULLS & COWS
  //   CS 21 PROJECT 1
  //   Jonathan Cancio 29
  //   Lorenzo Quiambao 48
  //   Input Display Digits
  //   BULLS
  //   Saved Setup Digits
  //   COWS
  //   WINS
  //   LIVES
endmodule
