// Logisim project JojoMemory.circ as structural Verilog: 9 circuits, main circuit main
module main (
  input  [2:0] in_1
);

  wire _0_out, _1_out, _2_out, _3_out, _4_out, _5_out, _6_out, _7_out, _8_out, _9_out, and_1_out,
       button_2_out, button_out, Clock, decoder_1_out0, decoder_1_out1, decoder_1_out2, decoder_1_out3,
       Enter_out, match_calculator_1_match, not_1_out, state_decoder_1_number_display,
       state_decoder_1_save_digits, state_decoder_1_update_wins_lives, undriven, undriven_2, undriven_3,
       undriven_4;
  wire [1:0] Digit_Selector;
  wire [2:0] match_calculator_1_bulls, match_calculator_1_cows, wins_lives_memory_1_lives;
  wire [3:0] bit_extender_1_out, bit_extender_2_out, bit_extender_3_out, D0, D1, D2, D3, S0, S1, S2, S3,
       wins_lives_memory_1_wins;

  Button _1 (.out(_1_out));
  Button _4 (.out(_4_out));
  Button _7 (.out(_7_out));
  Button button (.out(button_out));
  Clock clock_1 (.out(Clock));
  Button _3 (.out(_3_out));
  Button _2 (.out(_2_out));
  Button _5 (.out(_5_out));
  Button _6 (.out(_6_out));
  Button _8 (.out(_8_out));
  Button _9 (.out(_9_out));
  Button _0 (.out(_0_out));
  Button button_2 (.out(button_2_out));
  Button Enter (.out(Enter_out));
  Hex_Digit_Display hex_digit_display_1 (.value(S3));  // open: dp
  Hex_Digit_Display hex_digit_display_2 (.value(S2));  // open: dp
  digit_selector u_digit_selector (
    .L(button_out), .R(button_2_out), .Clock(Clock), .Enable(state_decoder_1_number_display),
    .out_5(Digit_Selector));
  Hex_Digit_Display hex_digit_display_3 (.value(S1));  // open: dp
  number_display number_display (
    ._0(_0_out), ._1(_1_out), ._2(_2_out), ._3(_3_out), ._4(_4_out), ._5(_5_out), ._6(_6_out), ._7(_7_out),
    ._8(_8_out), ._9(_9_out), .Clock(Clock), .in_13(Digit_Selector), .Enable(state_decoder_1_number_display),
    .D0(D0), .D1(D1), .D2(D2), .D3(D3));
  Hex_Digit_Display hex_digit_display_4 (.value(S0));  // open: dp
  saved_digits_memory saved_digits_memory_1 (
    .D0(D0), .D1(D1), .D2(D2), .D3(D3), .clock(Clock), .enable_save(and_1_out), .S0(S0), .S1(S1), .S2(S2),
    .S3(S3));
  Decoder #(.select(2)) decoder_1 (
    .out0(decoder_1_out0), .out1(decoder_1_out1), .out2(decoder_1_out2), .out3(decoder_1_out3),
    .sel(Digit_Selector));  // open: en
  and and_1 (and_1_out, state_decoder_1_save_digits, Enter_out);
  state_decoder state_decoder_1 (
    .state(in_1), .save_digits(state_decoder_1_save_digits),
    .update_wins_lives(state_decoder_1_update_wins_lives), .number_display(state_decoder_1_number_display));  // open: display_saved_number, bulls_cows, lives_count, wins_count, digit_select, start_led, game_led, wait_led, win_lose_led
  LED led_1 (.in(decoder_1_out3));
  Hex_Digit_Display hex_digit_display_5 (.value(D3));  // open: dp
  LED led_2 (.in(decoder_1_out2));
  Hex_Digit_Display hex_digit_display_6 (.value(D2));  // open: dp
  match_calculator match_calculator_1 (
    .D0(D0), .D1(D1), .D2(D2), .D3(D3), .S0(S0), .S1(S1), .S2(S2), .S3(S3), .match(match_calculator_1_match),
    .bulls(match_calculator_1_bulls), .cows(match_calculator_1_cows));
  LED led_3 (.in(decoder_1_out1));
  LED led_4 (.in(decoder_1_out0));
  Hex_Digit_Display hex_digit_display_7 (.value(D1));  // open: dp
  Hex_Digit_Display hex_digit_display_8 (.value(D0));  // open: dp
  Hex_Digit_Display hex_digit_display_9 (.value(bit_extender_1_out));  // open: dp
  assign bit_extender_1_out = {{1{1'b0}}, match_calculator_1_bulls};  // Bit_Extender bit_extender_1
  assign bit_extender_2_out = {{1{1'b0}}, match_calculator_1_cows};  // Bit_Extender bit_extender_2
  wins_lives_memory wins_lives_memory_1 (
    .match(match_calculator_1_match), .enable_update(state_decoder_1_update_wins_lives),
    .wins(wins_lives_memory_1_wins), .lives(wins_lives_memory_1_lives));
  Hex_Digit_Display hex_digit_display_10 (.value(bit_extender_2_out));  // open: dp
  LED Win (.in(undriven));
  not not_1 (not_1_out, undriven);
  LED Lose (.in(not_1_out));
  LED Start (.in(undriven_2));
  LED Game (.in(undriven_3));
  LED Wait (.in(undriven_4));
  Hex_Digit_Display hex_digit_display_11 (.value(wins_lives_memory_1_wins));  // open: dp
  Hex_Digit_Display hex_digit_display_12 (.value(bit_extender_3_out));  // open: dp
  assign bit_extender_3_out = {{1{1'b0}}, wins_lives_memory_1_lives};  // Bit_Extender bit_extender_3

  // Notes on the sheet:
  //   Inputs
  //   INSERT CIRCUIT HERE
  //   Outputs
  //   Bulls
  //   Cows
  //   Lives
  //   Wins
endmodule

module saved_digits_memory (
  input  [3:0] D0,
  input  [3:0] D1,
  input  [3:0] D2,
  input  [3:0] D3,
  input  clock,
  input  enable_save,
  output [3:0] S0,
  output [3:0] S1,
  output [3:0] S2,
  output [3:0] S3
);

  wire [3:0] controlled_buffer_1_out, controlled_buffer_2_out, controlled_buffer_3_out,
       controlled_buffer_4_out;

  assign controlled_buffer_1_out = enable_save ? D0 : 4'bz;  // Controlled_Buffer controlled_buffer_1
  assign controlled_buffer_2_out = enable_save ? D1 : 4'bz;  // Controlled_Buffer controlled_buffer_2
  assign controlled_buffer_3_out = enable_save ? D2 : 4'bz;  // Controlled_Buffer controlled_buffer_3
  assign controlled_buffer_4_out = enable_save ? D3 : 4'bz;  // Controlled_Buffer controlled_buffer_4
  Register #(.width(4)) register_1 (.D(controlled_buffer_1_out), .Q(S0), .clk(clock));  // open: en, clr
  Register #(.width(4)) register_2 (.D(controlled_buffer_2_out), .Q(S1), .clk(clock));  // open: en, clr
  Register #(.width(4)) register_3 (.D(controlled_buffer_3_out), .Q(S2), .clk(clock));  // open: en, clr
  Register #(.width(4)) register_4 (.D(controlled_buffer_4_out), .Q(S3), .clk(clock));  // open: en, clr
endmodule

module digit_selector (
  input  L,
  input  R,
  input  Enable,
  input  Clock,
  output [1:0] out_5
);

  wire and_1_out, and_2_out, and_3_out, and_4_out, and_5_out, and_6_out, and_7_out, and_8_out, and_9_out,
       not_1_out, not_2_out, not_3_out, not_4_out, not_5_out, not_6_out, not_7_out, not_8_out, not_9_out,
       not_10_out, not_11_out, not_12_out, not_13_out, not_14_out, or_1_out, or_2_out;
  wire [1:0] d_ff_2_q;

  not not_1 (not_1_out, R);
  not not_2 (not_2_out, L);
  not not_3 (not_3_out, R);
  not not_4 (not_4_out, d_ff_2_q[1]);
  not not_5 (not_5_out, d_ff_2_q[0]);
  not not_6 (not_6_out, L);
  not not_7 (not_7_out, d_ff_2_q[1]);
  not not_8 (not_8_out, d_ff_2_q[0]);
  not not_9 (not_9_out, R);
  not not_10 (not_10_out, L);
  and and_1 (and_1_out, not_9_out, not_10_out, d_ff_2_q[0]);
  not not_11 (not_11_out, R);
  and and_2 (and_2_out, not_11_out, L, not_12_out);
  not not_12 (not_12_out, d_ff_2_q[0]);
  and and_3 (and_3_out, R, not_13_out, not_14_out);
  not not_13 (not_13_out, L);
  not not_14 (not_14_out, d_ff_2_q[0]);
  and and_4 (and_4_out, R, L, d_ff_2_q[0]);
  and and_5 (and_5_out, not_1_out, not_2_out, d_ff_2_q[1]);
  and and_6 (and_6_out, not_3_out, L, not_4_out, d_ff_2_q[0]);
  and and_7 (and_7_out, L, d_ff_2_q[1], not_5_out);
  and and_8 (and_8_out, R, not_6_out, not_7_out, not_8_out);
  and and_9 (and_9_out, R, d_ff_2_q[1], d_ff_2_q[0]);
  or or_1 (or_1_out, and_1_out, and_2_out, and_3_out, and_4_out);
  or or_2 (or_2_out, and_5_out, and_6_out, and_7_out, and_8_out, and_9_out);
  D_Flip_Flop d_ff_1 (.clk(Clock), .D(or_2_out), .Q(d_ff_2_q[1]));  // open: Qn, preset, en, reset
  D_Flip_Flop d_ff_2 (.clk(Clock), .D(or_1_out), .Q(d_ff_2_q[0]));  // open: Qn, preset, en, reset
  assign out_5 = Enable ? d_ff_2_q : 2'bz;  // Controlled_Buffer controlled_buffer_1
endmodule

module number_display (
  input  _0,
  input  _1,
  input  _2,
  input  _3,
  input  _4,
  input  _5,
  input  _6,
  input  _7,
  input  _8,
  input  _9,
  input  Clock,
  input  Enable,
  input  [1:0] in_13,
  output [3:0] D0,
  output [3:0] D1,
  output [3:0] D2,
  output [3:0] D3
);

  wire and_1_out, and_2_out, and_3_out, and_4_out, and_5_out, Clock_T, decoder_1_out0, decoder_1_out1,
       decoder_1_out2, decoder_1_out3, priority_encoder_1_gs;
  wire [3:0] controlled_buffer_1_out, controlled_buffer_2_out, controlled_buffer_3_out,
       controlled_buffer_4_out, priority_encoder_1_out, register_1_q, register_2_q, register_3_q,
       register_4_q;

  Priority_Encoder #(.select(4)) priority_encoder_1 (
    .in0(_0), .in1(_1), .in2(_2), .in3(_3), .in4(_4), .in5(_5), .in6(_6), .in7(_7), .in8(_8), .in9(_9),
    .out(priority_encoder_1_out), .gs(priority_encoder_1_gs));  // open: in10, in11, in12, in13, in14, in15, en_out, en_in
  Clock clock_1 (.out(Clock_T));
  // Probe on priority_encoder_1_out
  assign controlled_buffer_1_out = and_1_out ? priority_encoder_1_out : 4'bz;  // Controlled_Buffer controlled_buffer_1
  assign controlled_buffer_2_out = and_2_out ? priority_encoder_1_out : 4'bz;  // Controlled_Buffer controlled_buffer_2
  assign controlled_buffer_3_out = and_3_out ? priority_encoder_1_out : 4'bz;  // Controlled_Buffer controlled_buffer_3
  assign controlled_buffer_4_out = and_4_out ? priority_encoder_1_out : 4'bz;  // Controlled_Buffer controlled_buffer_4
  Decoder #(.select(2)) decoder_1 (
    .out0(decoder_1_out0), .out1(decoder_1_out1), .out2(decoder_1_out2), .out3(decoder_1_out3), .sel(in_13));  // open: en
  Register #(.width(4)) register_1 (.D(controlled_buffer_1_out), .Q(register_1_q), .clk(Clock_T));  // open: en, clr
  and and_1 (and_1_out, and_5_out, decoder_1_out0);
  Register #(.width(4)) register_2 (.D(controlled_buffer_2_out), .Q(register_2_q), .clk(Clock_T));  // open: en, clr
  and and_2 (and_2_out, and_5_out, decoder_1_out1);
  Register #(.width(4)) register_3 (.D(controlled_buffer_3_out), .Q(register_3_q), .clk(Clock_T));  // open: en, clr
  and and_3 (and_3_out, and_5_out, decoder_1_out2);
  Register #(.width(4)) register_4 (.D(controlled_buffer_4_out), .Q(register_4_q), .clk(Clock_T));  // open: en, clr
  and and_4 (and_4_out, and_5_out, decoder_1_out3);
  and and_5 (and_5_out, Enable, priority_encoder_1_gs);
  assign D0 = Enable ? register_1_q : 4'bz;  // Controlled_Buffer controlled_buffer_5
  assign D1 = Enable ? register_2_q : 4'bz;  // Controlled_Buffer controlled_buffer_6
  assign D2 = Enable ? register_3_q : 4'bz;  // Controlled_Buffer controlled_buffer_7
  assign D3 = Enable ? register_4_q : 4'bz;  // Controlled_Buffer controlled_buffer_8
endmodule

module bulls_calculator (
  input  [3:0] D0,
  input  [3:0] D1,
  input  [3:0] D2,
  input  [3:0] D3,
  input  [3:0] S0,
  input  [3:0] S1,
  input  [3:0] S2,
  input  [3:0] S3,
  output [2:0] bulls
);

  wire comparator_1_eq, comparator_2_eq, comparator_3_eq, comparator_4_eq;

  Comparator #(.width(4)) comparator_1 (.a(D0), .b(S0), .eq(comparator_1_eq));  // open: gt, lt
  Comparator #(.width(4)) comparator_2 (.a(D1), .b(S1), .eq(comparator_2_eq));  // open: gt, lt
  Comparator #(.width(4)) comparator_3 (.a(D2), .b(S2), .eq(comparator_3_eq));  // open: gt, lt
  Comparator #(.width(4)) comparator_4 (.a(D3), .b(S3), .eq(comparator_4_eq));  // open: gt, lt
  BitAdder #(.width(1)) bitadder_1 (
    .in0(comparator_1_eq), .in1(comparator_2_eq), .in2(comparator_3_eq), .in3(comparator_4_eq), .out(bulls));
endmodule

module cows_calculator (
  input  [3:0] D0,
  input  [3:0] D1,
  input  [3:0] D2,
  input  [3:0] D3,
  input  [3:0] S0,
  input  [3:0] S1,
  input  [3:0] S2,
  input  [3:0] S3,
  output [2:0] cows
);

  wire comparator_1_eq, comparator_2_eq, comparator_3_eq, comparator_4_eq, comparator_5_eq, comparator_6_eq,
       comparator_7_eq, comparator_8_eq, comparator_9_eq, comparator_10_eq, comparator_11_eq,
       comparator_12_eq, or_1_out, or_2_out, or_3_out, or_4_out;

  Comparator #(.width(4)) comparator_1 (.a(D1), .b(S0), .eq(comparator_1_eq));  // open: gt, lt
  Comparator #(.width(4)) comparator_2 (.a(D2), .b(S0), .eq(comparator_2_eq));  // open: gt, lt
  Comparator #(.width(4)) comparator_3 (.a(D3), .b(S0), .eq(comparator_3_eq));  // open: gt, lt
  Comparator #(.width(4)) comparator_4 (.a(D0), .b(S1), .eq(comparator_4_eq));  // open: gt, lt
  Comparator #(.width(4)) comparator_5 (.a(D2), .b(S1), .eq(comparator_5_eq));  // open: gt, lt
  Comparator #(.width(4)) comparator_6 (.a(D3), .b(S1), .eq(comparator_6_eq));  // open: gt, lt
  Comparator #(.width(4)) comparator_7 (.a(D0), .b(S2), .eq(comparator_7_eq));  // open: gt, lt
  Comparator #(.width(4)) comparator_8 (.a(D1), .b(S2), .eq(comparator_8_eq));  // open: gt, lt
  Comparator #(.width(4)) comparator_9 (.a(D3), .b(S2), .eq(comparator_9_eq));  // open: gt, lt
  Comparator #(.width(4)) comparator_10 (.a(D0), .b(S3), .eq(comparator_10_eq));  // open: gt, lt
  Comparator #(.width(4)) comparator_11 (.a(D1), .b(S3), .eq(comparator_11_eq));  // open: gt, lt
  Comparator #(.width(4)) comparator_12 (.a(D2), .b(S3), .eq(comparator_12_eq));  // open: gt, lt
  or or_1 (or_1_out, comparator_1_eq, comparator_2_eq, comparator_3_eq);
  or or_2 (or_2_out, comparator_4_eq, comparator_5_eq, comparator_6_eq);
  or or_3 (or_3_out, comparator_7_eq, comparator_8_eq, comparator_9_eq);
  or or_4 (or_4_out, comparator_10_eq, comparator_11_eq, comparator_12_eq);
  BitAdder #(.width(1)) bitadder_1 (.in0(or_1_out), .in1(or_2_out), .in2(or_3_out), .in3(or_4_out), .out(cows));
endmodule

module state_decoder (
  input  [2:0] state,
  output update_wins_lives,
  output display_saved_number,
  output save_digits,
  output number_display,
  output bulls_cows,
  output lives_count,
  output wins_count,
  output digit_select,
  output start_led,
  output game_led,
  output wait_led,
  output win_lose_led
);

  wire and_4_out, and_5_out, and_6_out, and_7_out, and_9_out, and_10_out, and_11_out, and_12_out, and_13_out,
       and_14_out, and_15_out, and_16_out, and_17_out, and_18_out, and_19_out, and_20_out, and_21_out,
       not_1_out, not_2_out, not_3_out, not_4_out, not_5_out, not_6_out, not_7_out, not_8_out, not_9_out,
       not_10_out, not_11_out, not_12_out, not_13_out, not_14_out, not_15_out, not_16_out, not_17_out,
       not_18_out, not_19_out, not_20_out, not_21_out, not_22_out, not_23_out, not_24_out, not_25_out,
       not_26_out;

  and and_1 (save_digits, ~state[2], ~state[1], ~state[0]);  // AND_Gate
  and and_2 (update_wins_lives, state[2], ~state[1], ~state[0]);  // AND_Gate
  and and_3 (display_saved_number, state[2], ~state[1], state[0]);  // AND_Gate
  not not_1 (not_1_out, state[0]);
  not not_2 (not_2_out, state[1]);
  not not_3 (not_3_out, state[2]);
  not not_4 (not_4_out, state[0]);
  not not_5 (not_5_out, state[1]);
  not not_6 (not_6_out, state[2]);
  not not_7 (not_7_out, state[0]);
  not not_8 (not_8_out, state[0]);
  not not_9 (not_9_out, state[1]);
  not not_10 (not_10_out, state[2]);
  not not_11 (not_11_out, state[0]);
  not not_12 (not_12_out, state[1]);
  not not_13 (not_13_out, state[2]);
  not not_14 (not_14_out, state[0]);
  not not_15 (not_15_out, state[0]);
  not not_16 (not_16_out, state[1]);
  not not_17 (not_17_out, state[0]);
  not not_18 (not_18_out, state[2]);
  not not_19 (not_19_out, state[0]);
  not not_20 (not_20_out, state[1]);
  not not_21 (not_21_out, state[2]);
  not not_22 (not_22_out, state[0]);
  not not_23 (not_23_out, state[1]);
  not not_24 (not_24_out, state[2]);
  not not_25 (not_25_out, state[1]);
  not not_26 (not_26_out, state[2]);
  and and_4 (and_4_out, not_1_out, not_2_out, not_3_out);
  and and_5 (and_5_out, not_4_out, state[1], state[2]);
  and and_6 (and_6_out, state[0], not_5_out, state[2]);
  and and_7 (and_7_out, state[0], state[1], not_6_out);
  and and_8 (bulls_cows, not_7_out, state[1], state[2]);
  and and_9 (and_9_out, not_8_out, state[1], state[2]);
  or or_1 (lives_count, and_9_out, and_10_out, and_11_out);
  and and_10 (and_10_out, state[0], not_9_out, state[2]);
  and and_11 (and_11_out, state[0], state[1], not_10_out);
  and and_12 (and_12_out, not_11_out, not_12_out, not_13_out);
  or or_2 (digit_select, and_12_out, and_13_out);
  and and_13 (and_13_out, not_14_out, state[1], state[2]);
  and and_14 (and_14_out, not_15_out, not_16_out);
  or or_3 (start_led, and_14_out, and_15_out);
  and and_15 (and_15_out, not_17_out, not_18_out);
  and and_16 (and_16_out, not_19_out, state[1], state[2]);
  or or_4 (game_led, and_16_out, and_17_out);
  and and_17 (and_17_out, state[0], not_20_out, not_21_out);
  and and_18 (and_18_out, not_22_out, not_23_out, state[2]);
  or or_5 (wait_led, and_18_out, and_19_out);
  and and_19 (and_19_out, state[0], not_24_out);
  and and_20 (and_20_out, state[0], not_25_out, state[2]);
  or or_6 (win_lose_led, and_20_out, and_21_out);
  and and_21 (and_21_out, state[0], state[1], not_26_out);
  or or_7 (number_display, and_4_out, and_5_out, and_6_out, and_7_out);

  assign wins_count = 1'b1;
endmodule

module wins_lives_memory (
  input  match,
  input  enable_update,
  output [3:0] wins,
  output [2:0] lives
);

  wire and_1_out, and_2_out, clock_1_out, not_1_out;
  wire [2:0] controlled_buffer_2_out, subtractor_1_out;
  wire [3:0] adder_1_out, controlled_buffer_1_out;

  not not_1 (not_1_out, match);
  Adder #(.width(4)) adder_1 (.a(wins), .b(4'b0001), .out(adder_1_out));  // open: cin, cout
  Subtractor #(.width(3)) subtractor_1 (.a(lives), .b(3'b001), .out(subtractor_1_out));  // open: bin, bout
  assign controlled_buffer_1_out = and_1_out ? adder_1_out : 4'bz;  // Controlled_Buffer controlled_buffer_1
  and and_1 (and_1_out, match, enable_update);
  assign controlled_buffer_2_out = and_2_out ? subtractor_1_out : 3'bz;  // Controlled_Buffer controlled_buffer_2
  and and_2 (and_2_out, not_1_out, enable_update);
  Register #(.width(4)) u_wins (.D(controlled_buffer_1_out), .Q(wins), .clk(clock_1_out));  // open: en, clr
  Register #(.width(3)) u_lives (.D(controlled_buffer_2_out), .Q(lives), .clk(clock_1_out));  // open: en, clr
  Clock clock_1 (.out(clock_1_out));
endmodule

module match_calculator (
  input  [3:0] D0,
  input  [3:0] D1,
  input  [3:0] D2,
  input  [3:0] D3,
  input  [3:0] S0,
  input  [3:0] S1,
  input  [3:0] S2,
  input  [3:0] S3,
  output match,
  output [2:0] bulls,
  output [2:0] cows
);

  bulls_calculator bulls_calculator_1 (
    .D0(D0), .D1(D1), .D2(D2), .D3(D3), .S0(S0), .S1(S1), .S2(S2), .S3(S3), .bulls(bulls));
  cows_calculator cows_calculator_1 (
    .D0(D0), .D1(D1), .D2(D2), .D3(D3), .S0(S0), .S1(S1), .S2(S2), .S3(S3), .cows(cows));
  Comparator #(.width(3)) comparator_1 (.a(bulls), .b(3'b100), .eq(match));  // open: gt, lt
endmodule
