// Logisim project Mik_circuit.circ as structural Verilog
module Circuit_Controller (
  input  lives,
  input  win,
  input  enter,
  input  Clock,
  output out_5
);

  wire and_1_out, and_2_out, and_3_out, and_4_out, and_5_out, and_6_out, and_7_out, and_8_out, and_9_out,
       and_10_out, and_11_out, and_12_out, and_13_out, and_14_out, not_1_out, not_2_out, not_3_out,
       not_4_out, not_5_out, not_6_out, not_7_out, not_8_out, not_9_out, not_10_out, not_11_out, not_12_out,
       not_13_out, not_14_out, not_15_out, not_16_out, not_17_out, not_18_out, not_19_out, not_20_out,
       not_21_out, or_1_out, or_2_out, or_3_out, undriven;
  wire [2:0] D1_q;

  not not_1 (not_1_out, D1_q[1]);
  not not_2 (not_2_out, D1_q[0]);
  not not_3 (not_3_out, D1_q[2]);
  not not_4 (not_4_out, D1_q[1]);
  not not_5 (not_5_out, D1_q[1]);
  not not_6 (not_6_out, enter);
  not not_7 (not_7_out, D1_q[2]);
  not not_8 (not_8_out, enter);
  not not_9 (not_9_out, D1_q[2]);
  not not_10 (not_10_out, lives);
  not not_11 (not_11_out, win);
  not not_12 (not_12_out, D1_q[1]);
  not not_13 (not_13_out, D1_q[0]);
  not not_14 (not_14_out, D1_q[1]);
  not not_15 (not_15_out, D1_q[0]);
  not not_16 (not_16_out, enter);
  not not_17 (not_17_out, D1_q[2]);
  not not_18 (not_18_out, enter);
  not not_19 (not_19_out, D1_q[1]);
  not not_20 (not_20_out, D1_q[0]);
  not not_21 (not_21_out, D1_q[0]);
  and and_1 (and_1_out, D1_q[2], not_1_out, D1_q[0]);
  and and_2 (and_2_out, D1_q[2], D1_q[1], not_2_out);
  and and_3 (and_3_out, enter, not_3_out, D1_q[1], D1_q[0]);
  and and_4 (and_4_out, win, D1_q[2], not_4_out);
  and and_5 (and_5_out, lives, D1_q[2], not_5_out);
  and and_6 (and_6_out, not_6_out, not_7_out, D1_q[0]);
  and and_7 (and_7_out, not_8_out, not_9_out, D1_q[1]);
  and and_8 (and_8_out, not_10_out, not_11_out, D1_q[2], not_12_out, not_13_out);
  and and_9 (and_9_out, enter, not_14_out, D1_q[0]);
  and and_10 (and_10_out, enter, D1_q[1], not_15_out);
  and and_11 (and_11_out, not_16_out, not_17_out, D1_q[1]);
  and and_12 (and_12_out, not_18_out, D1_q[2], not_19_out);
  and and_13 (and_13_out, D1_q[2], not_20_out);
  and and_14 (and_14_out, enter, not_21_out);
  or or_1 (or_1_out, and_1_out, and_2_out, and_3_out, and_4_out, and_5_out);
  or or_2 (or_2_out, and_6_out, and_7_out, and_8_out, and_9_out, and_10_out);
  or or_3 (or_3_out, and_11_out, and_12_out, and_13_out, and_14_out);
  D_Flip_Flop D3 (.clk(undriven), .D(or_1_out), .Q(D1_q[2]));  // open: Qn, preset, en, reset
  D_Flip_Flop D2 (.clk(undriven), .D(or_2_out), .Q(D1_q[1]));  // open: Qn, preset, en, reset
  D_Flip_Flop D1 (.clk(undriven), .D(or_3_out), .Q(D1_q[0]));  // open: Qn, preset, en, reset
endmodule
